# Fritzing sketch temperature_control_gh (saved by Fritzing 0.9.3b)
breadboards: 1
perfboards: 1

parts:
  SG1 = Buzzer 12mm [package=buzzer-12mm-ns]
  S1 = Pushbutton [package="[THT]"]
  S2 = Pushbutton [package="[THT]"]
  S3 = Pushbutton [package="[THT]"]
  R3 = Rotary Potentiometer (Small) [maximum_resistance=10kΩ package=THT]
  DS1 = DS18B20 1-Wire Temperature Sensor [part_number=DS18B20]
  R4 = Resistor [tolerance=±5% resistance=220 package="1206 [SMD]"]
  R5 = Resistor [tolerance=±5% resistance=4.7k package="1206 [SMD]"]
  LED1 = LED - 3mm [color="Red (633nm)" package="3 mm [THT]"]
  R6 = Resistor [tolerance=±5% resistance=220 package="1206 [SMD]"]
  J2 = Generic rounded female header - 5 pins [form="♀ (female rounded)" package=THT]
  Part2 = Arduino Nano (Rev3.0)

nets:
  N1: SG1.1, Part2.D3
  N2: SG1.2, R4.Pin_1
  N3: S1.Pin_1, S1.Pin_2, Part2.A2
  GND: S1.Pin_3, S1.Pin_4, S2.Pin_3, S2.Pin_4, S3.Pin_3, S3.Pin_4, R3.leg2, DS1.GND, R4.Pin_0, R6.Pin_1, J2.GND, Part2.GND
  N4: S2.Pin_1, S2.Pin_2, Part2.A1
  N5: S3.Pin_1, S3.Pin_2, Part2.A0
  VDD: R3.leg1, DS1.VDD, R5.Pin_1, J2.VCC, Part2.5V
  N6: R3.wiper, Part2.A3
  N7: DS1.DQ, R5.Pin_0, Part2.D4
  N8: LED1.cathode, R6.Pin_0
  N9: LED1.anode, Part2.D5
  N10: J2.SR_CLOCK, Part2.D8
  N11: J2.SR_LATCH, Part2.D9
  N12: J2.SR_DATA, Part2.D10

custom parts:
  Generic rounded female header - 5 pins: Generic rounded female header
